// Logisim project practs.circ as structural Verilog: 1 circuit, main circuit main
module main (
  input  in_1,
  input  in_2,
  input  in_3,
  input  in_4,
  input  in_5,
  input  in_6,
  input  in_7,
  input  in_8,
  input  in_9,
  input  in_10,
  input  in_11,
  output out_12,
  output out_13,
  output out_14,
  output out_15,
  output out_16,
  output out_17,
  output out_18,
  output out_19,
  output out_20,
  output out_21,
  output out_22,
  output out_23
);

  wire and_2_out, and_3_out, and_4_out, clock_1_out, clock_2_out, clock_3_out, clock_4_out, clock_5_out,
       j_k_ff_2_qn, j_k_ff_6_qn, j_k_ff_8_qn, nand_1_out, nand_2_out, nand_3_out, nand_4_out, nand_5_out,
       nand_6_out, not_1_out, xor_2_out;

  Clock clock_1 (.out(clock_1_out));
  Clock clock_2 (.out(clock_2_out));
  Clock clock_3 (.out(clock_3_out));
  J_K_Flip_Flop j_k_ff_1 (.J(in_5), .clk(clock_2_out), .K(in_5), .Q(out_15));  // open: Qn, preset, en, reset
  not not_1 (not_1_out, clock_1_out);
  nand nand_1 (nand_1_out, out_13, in_1, clock_1_out);
  nand nand_2 (nand_2_out, clock_1_out, in_2, out_12);
  J_K_Flip_Flop j_k_ff_2 (.J(in_4), .clk(clock_3_out), .K(in_4), .Qn(j_k_ff_2_qn));  // open: Q, preset, en, reset
  xor xor_1 (out_20, in_8, in_10);
  J_K_Flip_Flop j_k_ff_3 (.J(out_15), .clk(clock_2_out), .K(out_15), .Q(out_14));  // open: Qn, preset, en, reset
  and and_1 (out_22, in_8, in_10);
  nand nand_3 (nand_3_out, nand_1_out, nand_4_out);
  nand nand_4 (nand_4_out, nand_3_out, nand_2_out);
  and and_2 (and_2_out, out_15, out_14);
  J_K_Flip_Flop j_k_ff_4 (.J(in_4), .clk(j_k_ff_2_qn), .K(in_4));  // open: Q, Qn, preset, en, reset
  Clock clock_4 (.out(clock_4_out));
  J_K_Flip_Flop j_k_ff_5 (.J(and_2_out), .clk(clock_2_out), .K(and_2_out), .Q(out_16));  // open: Qn, preset, en, reset
  nand nand_5 (nand_5_out, nand_3_out, not_1_out);
  nand nand_6 (nand_6_out, not_1_out, nand_4_out);
  J_K_Flip_Flop j_k_ff_6 (.J(in_3), .clk(clock_4_out), .K(in_3), .Qn(j_k_ff_6_qn));  // open: Q, preset, en, reset
  Clock clock_5 (.out(clock_5_out));
  xor xor_2 (xor_2_out, in_7, in_9);
  J_K_Flip_Flop j_k_ff_7 (.J(in_6), .clk(clock_5_out), .K(in_6), .Q(out_17));  // open: Qn, preset, en, reset
  nand nand_7 (out_12, nand_5_out, out_13);
  nand nand_8 (out_13, out_12, nand_6_out);
  J_K_Flip_Flop j_k_ff_8 (.J(in_3), .clk(j_k_ff_6_qn), .K(in_3), .Qn(j_k_ff_8_qn));  // open: Q, preset, en, reset
  xor xor_3 (out_21, xor_2_out, in_11);
  J_K_Flip_Flop j_k_ff_9 (.J(in_3), .clk(j_k_ff_8_qn), .K(in_3));  // open: Q, Qn, preset, en, reset
  J_K_Flip_Flop j_k_ff_10 (
    .J(out_17), .clk(clock_5_out), .K(out_17), .Q(out_18), .Qn(out_19));  // open: preset, en, reset
  and and_3 (and_3_out, xor_2_out, in_11);
  and and_4 (and_4_out, in_9, in_7);
  or or_1 (out_23, and_3_out, and_4_out);

  // Notes on the sheet:
  //   2/3 bit sync counter
  //   2/3 bit async counter
  //   JK Mater Slave 
endmodule
